// Logisim project decoder.circ as structural Verilog: 1 circuit, main circuit main
module main (
  input  x,
  input  y
);

  wire and_1_out, not_1_out;

  not not_1 (not_1_out, x);
  and and_1 (and_1_out, y, not_1_out);
  _7_Segment_Display u_7_segment_display_1 (.b(and_1_out));  // open: g, f, a, e, d, c, dp
endmodule
